// Logisim project LAB4Final.circ as structural Verilog: 14 circuits, main circuit Main
module Main (
);

  wire ALUSrc, ALUSrcF, ALUZero, ALUZeroIn, Branch, BranchF, BranchTaken, clear, CLK, Ex_Branch, Ex_Jump,
       Ex_MemRead, Ex_MemWrite, Ex_RegWrite, JRbit, Jump, JumpF, MEM_RegWrite, MemRdF, MemRead, MemWrite,
       MemWriteF, not_1_out, RegWrite, RegWriteF, Stall;
  wire [1:0] EX_MemToReg, ForwardA, ForwardB, MEM_MemToReg, MemToReg, MemToRegF, RegDst, RegDstF;
  wire [3:0] ALUControl, ALUControlF;
  wire [4:0] Ex_Rd, Ex_Rs, Ex_Rt, MEM_wrAddr, SHAMTF, wrAddr, wrAddrF;
  wire [5:0] FUNC;
  wire [13:0] controlunit_1_out_2;
  wire [27:0] shifter_3_out;
  wire [31:0] A, ALUA, ALUB, B, Bin, Bout, Din, Dout1, Ex_Inst, Ex_PC, Ex_PC2, Ex_PCout, ID_PC, imm, InstF,
       InstImm, JumpPC, MEM_PC, MEM_PC2, mem_wb_1_out_11, mem_wb_1_out_12, Min, multiplexer_6_out, PC_4,
       PC_q, PCin, RdData1, RdData2, rom_1_data, shifter_1_out, WB_PC, WRData;
  wire [31:6] Inst;

  // Probe on Inst[31:26]
  Register #(.width(32)) PC (.D(PCin), .en(not_1_out), .Q(PC_q), .clk(CLK));  // open: clr
  not not_1 (not_1_out, Stall);
  // Probe on Inst[25:21]
  Clock clock_1 (.out(CLK));
  Adder #(.width(32)) adder_1 (.a(32'h4), .b(PC_q), .out(PC_4));  // open: cin, cout
  // Probe on Inst[10:6]
  // Probe on Inst[20:16]
  // Probe on Inst[15:11]
  // Probe on FUNC
  IF_ID if_id_1 (
    .PC_4(PC_4), .PC(rom_1_data), .Stall(not_1_out), .Clock(CLK), .Branch(clear), .PC_4out(ID_PC),
    .INSTout({Inst, FUNC}));
  ROM #(.dataWidth(32)) rom_1 (.addr(PC_q[9:2]), .data(rom_1_data));  // open: sel
  // Probe on Inst[31:26]
  // Probe on Inst[25:21]
  // Probe on Inst[20:16]
  // Probe on {Inst[15:6], FUNC}
  assign InstImm = {{16{1'b0}}, {Inst[15:6], FUNC}};  // Bit_Extender bit_extender_1
  Hazard_Unit hazard_unit_1 (
    .ID_EX_MemRead(Ex_MemRead), .ID_EX_RegisterRt(Ex_Rt), .IF_ID_RegisterRs(Inst[25:21]),
    .IF_ID_RegisterRt(Inst[20:16]), .Stall(Stall));
  Register_File register_file_1 (
    .WrAddr(wrAddrF), .WrData(WRData), .WrReg(RegWriteF), .RdAddr1(Inst[25:21]), .RdAddr2(Inst[20:16]),
    .RdData1(RdData1), .RdData2(RdData2), .Clock(CLK));
  Multiplexer #(.select(2), .width(32)) multiplexer_1 (
    .in0(A), .in1(WRData), .in2(Dout1), .out(ALUA), .sel(ForwardA));  // open: in3, en
  Multiplexer #(.select(2), .width(32)) multiplexer_2 (
    .in0(B), .in1(WRData), .in2(Dout1), .out(Bin), .sel(ForwardB));  // open: in3, en
  ID_EX id_ex_1 (
    .ALUSrc(ALUSrc), .ALUControl(ALUControl), .MemToReg(MemToReg), .Branch(Branch), .Jump(Jump),
    .Inst({Inst, FUNC}), .ID_PC(ID_PC), .ID_PC_2(ID_PC), .RdData1(RdData1), .RdData2(RdData2),
    .instImm(InstImm), .rd(Inst[15:11]), .rt(Inst[20:16]), .rs(Inst[25:21]), .RegWrite(RegWrite),
    .MemWrite(MemWrite), .MemRead(MemRead), .RegDst(RegDst), .shamt(Inst[10:6]), .Clock(CLK), .Clear(clear),
    .out_22(ALUSrcF), .out_23(ALUControlF), .out_24(EX_MemToReg), .out_25(Ex_Branch), .out_26(Ex_Jump),
    .out_27(Ex_Inst), .out_28(Ex_PC), .out_29(Ex_PC2), .out_30(A), .out_31(B), .out_32(imm), .out_33(Ex_Rd),
    .out_34(Ex_Rt), .out_35(Ex_Rs), .out_36(Ex_RegWrite), .out_37(Ex_MemWrite), .out_38(Ex_MemRead),
    .RegDstF(RegDstF), .out_40(SHAMTF));
  Multiplexer #(.width(32)) multiplexer_3 (.in0(Bin), .in1(imm), .out(ALUB), .sel(ALUSrcF));  // open: en
  Shifter #(.width(32)) shifter_1 (.in(InstImm), .\dist (5'b00010), .out(shifter_1_out));
  ALU alu_1 (
    .ALUCtl(ALUControlF), .A(ALUA), .B(ALUB), .ALUResult(Din), .Zero(ALUZeroIn), .Shamt(SHAMTF));  // open: Overflow
  Adder #(.width(32)) adder_2 (.a(Ex_PC), .b(shifter_1_out), .out(Ex_PCout));  // open: cin, cout
  Multiplexer #(.select(2), .width(5)) multiplexer_4 (
    .in0(Ex_Rt), .in1(Ex_Rd), .in2({5{1'b1}}), .out(wrAddr), .sel(RegDstF));  // open: in3, en
  Forwarding_Unit forwarding_unit_1 (
    .EX_MEM_RegWrite(MEM_RegWrite), .EX_MEM_RegisterRd(MEM_wrAddr), .ID_EX_RegisterRs(Ex_Rs),
    .MEM_WB_RegWrite(RegWriteF), .MEM_WB_RegisterRd(wrAddrF), .ID_EX_RegisterRt(Ex_Rt), .ForwardA(ForwardA),
    .ForwardB(ForwardB));
  ControlUnit controlunit_1 (.InstructionIN({Inst, FUNC}), .out_2(controlunit_1_out_2));
  Multiplexer #(.width(14)) multiplexer_5 (
    .in0(controlunit_1_out_2), .in1({14{1'b0}}),
    .out({RegDst, Jump, Branch, MemRead, MemToReg, ALUControl, MemWrite, ALUSrc, RegWrite}), .sel(Stall));  // open: en
  EX_MEM ex_mem_1 (
    .MemToReg(EX_MemToReg), .Branch(Ex_Branch), .Jump(Ex_Jump), .Inst(Ex_Inst), .Ex_PC(Ex_PCout),
    .Ex_PC2(Ex_PC2), .Ex_WriteAddr(wrAddr), .ALUZero(ALUZeroIn), .Din(Din), .Bin(Bin),
    .RegWrite(Ex_RegWrite), .MemWrite(Ex_MemWrite), .MemRead(Ex_MemRead), .Clock(CLK), .out_15(MEM_MemToReg),
    .out_16(BranchF), .out_17(JumpF), .out_18(InstF), .out_19(MEM_PC), .out_20(MEM_PC2), .out_21(MEM_wrAddr),
    .out_22(ALUZero), .out_23(Dout1), .out_24(Bout), .out_25(MEM_RegWrite), .out_26(MemWriteF),
    .out_27(MemRdF));
  and and_1 (BranchTaken, BranchF, ALUZero);
  Multiplexer #(.width(32)) multiplexer_6 (
    .in0(PC_4), .in1(MEM_PC), .out(multiplexer_6_out), .sel(BranchTaken));  // open: en
  Shifter #(.width(32)) shifter_2 (.in(Dout1), .\dist (5'b00010), .out(JumpPC));
  JR jr_1 (
    .Function(InstF[5:0]), .Shiftamt(InstF[10:6]), .rd(InstF[15:11]), .rt(InstF[20:16]),
    .Opcode(InstF[31:26]), .JR(JRbit));
  Shifter #(.width(28)) shifter_3 (.in(InstF[27:0]), .\dist (5'b00010), .out(shifter_3_out));
  RAM #(.dataWidth(32), .bus("separate")) ram_1 (
    .addr(Dout1[7:0]), .din(Bout), .data(Min), .str(MemWriteF), .clk(CLK), .ld(MemRdF));  // open: sel, clr
  or or_1 (clear, JumpF, BranchTaken);
  Multiplexer #(.select(2), .width(32)) multiplexer_7 (
    .in0(multiplexer_6_out), .in1({PC_4[31:28], shifter_3_out}), .in2(JumpPC), .in3(Dout1), .out(PCin),
    .sel({JRbit, JumpF}));  // open: en
  MEM_WB mem_wb_1 (
    .MemToReg(MEM_MemToReg), .MEM_PC2(MEM_PC2), .MEM_WriteAddr(MEM_wrAddr), .Dout1(Dout1), .Min(Min),
    .RegWrite(MEM_RegWrite), .Clock(CLK), .out_8(MemToRegF), .out_9(WB_PC), .out_10(wrAddrF),
    .out_11(mem_wb_1_out_11), .out_12(mem_wb_1_out_12), .out_13(RegWriteF));
  Multiplexer #(.select(2), .width(32)) multiplexer_8 (
    .in0(mem_wb_1_out_11), .in1(mem_wb_1_out_12), .in2(WB_PC), .out(WRData), .sel(MemToRegF));  // open: in3, en
  // Probe on nothing
  // Probe on nothing
  // Probe on nothing
  // Probe on nothing
  // Probe on nothing
  // Probe on nothing
  // Probe on nothing
  // Probe on nothing
  // Probe on nothing
  // Probe on nothing

  // Other names for the same wires on the sheet: Douttt[31:0] = Dout1; Inst[5:0] = FUNC; SHAMT[4:0] = Inst[10:6];
  //   rd[4:0] = Inst[15:11]; rt[4:0] = Inst[20:16]; rs[4:0] = Inst[25:21]; OpCode[5:0] = Inst[31:26];
  //   MEM_FUNC[5:0] = InstF[5:0]; MEM_SHAMT[4:0] = InstF[10:6]; MEM_rd[4:0] = InstF[15:11];
  //   MEM_rt[4:0] = InstF[20:16]; MEM_rs[4:0] = InstF[25:21]; MEM_OpCode[5:0] = InstF[31:26]

  // Notes on the sheet:
  //   contents of rom_1 (hex, n*v repeats v):
  //   34010001 211020 221826 2064000e 232822 aca4000e 8ca6000e c43824 10e10003 c7402a 11080001 20110001
  //   20090001 8c0a000c ad4a0013 8c0a000c 1141fffb c000013 20120001 23ff002c ac1f0000 308b0010 456027
  //   446825 97140 27842 8c100000 2000008 20130001 800001d 20140001 20150001
endmodule

module ALU (
  input  [3:0] ALUCtl,
  input  [31:0] A,
  input  [31:0] B,
  input  [4:0] Shamt,
  output [31:0] ALUResult,
  output Zero,
  output Overflow
);

  wire comparator_1_lt, comparator_2_lt, comparator_3_eq, comparator_4_eq, or_2_out;
  wire [31:0] ADD, AND, NOR, OR, SLL, SLT, SLTU, SRL, SUB, XOR;

  assign XOR = A ^ B;  // XOR_Gate xor_1, 32 bits wide
  Adder #(.width(32)) adder_1 (.a(A), .b(B), .out(ADD));  // open: cin, cout
  Subtractor #(.width(32)) subtractor_1 (.a(A), .b(B), .out(SUB));  // open: bin, bout
  assign AND = A & B;  // AND_Gate and_1, 32 bits wide
  assign OR = A | B;  // OR_Gate or_1, 32 bits wide
  assign NOR = ~(A | B);  // NOR_Gate nor_1, 32 bits wide
  Comparator #(.width(32)) comparator_1 (.a(A), .b(B), .lt(comparator_1_lt));  // open: gt, eq
  assign SLT = {{31{1'b0}}, comparator_1_lt};  // Bit_Extender bit_extender_1
  Shifter #(.width(32)) shifter_1 (.in(B), .\dist (Shamt), .out(SLL));
  Shifter #(.width(32), .shift("lr")) shifter_2 (.in(B), .\dist (Shamt), .out(SRL));
  Comparator #(.width(32), .mode("unsigned")) comparator_2 (.a(A), .b(B), .lt(comparator_2_lt));  // open: gt, eq
  assign SLTU = {{31{1'b0}}, comparator_2_lt};  // Bit_Extender bit_extender_2
  Multiplexer #(.select(4), .width(32), .enable("false")) multiplexer_1 (
    .in0(ADD), .in1(SUB), .in2(AND), .in3(OR), .in4(NOR), .in5(XOR), .in6(SLT), .in14(SLL), .in15(SRL),
    .out(ALUResult), .sel(ALUCtl));  // open: in7, in8, in9, in10, in11, in12, in13
  Comparator #(.width(4)) comparator_3 (.a(4'b0000), .b(ALUCtl), .eq(comparator_3_eq));  // open: gt, lt
  Comparator #(.width(4)) comparator_4 (.a(ALUCtl), .b(4'b0001), .eq(comparator_4_eq));  // open: gt, lt
  Overflow_Unit overflow_unit_1 (
    .Add(comparator_3_eq), .Sub(comparator_4_eq), .ASign(A[31]), .BSign(B[31]), .ResultSign(ALUResult[31]),
    .Overflow(Overflow));
  not not_1 (Zero, or_2_out);
  or or_2 (or_2_out, ALUResult[0], ALUResult[1], ALUResult[2], ALUResult[3], ALUResult[4], ALUResult[5], ALUResult[6], ALUResult[7], ALUResult[8], ALUResult[9], ALUResult[10], ALUResult[11], ALUResult[12], ALUResult[13], ALUResult[14], ALUResult[15], ALUResult[16], ALUResult[17], ALUResult[18], ALUResult[19], ALUResult[20], ALUResult[21], ALUResult[22], ALUResult[23], ALUResult[24], ALUResult[25], ALUResult[26], ALUResult[27], ALUResult[28], ALUResult[29], ALUResult[30], ALUResult[31]);

  // Other names for the same wires on the sheet: ASign = A[31]; ResultSign = ALUResult[31]; BSign = B[31]

  // Notes on the sheet:
  //   ALUCtl for ADD on top port
  //   ALUCtl for SUB on second port
endmodule

module Register_File (
  input  [4:0] WrAddr,
  input  [31:0] WrData,
  input  WrReg,
  input  [4:0] RdAddr1,
  input  [4:0] RdAddr2,
  input  Clock,
  output [31:0] RdData1,
  output [31:0] RdData2
);

  wire and_1_out, and_2_out, comparator_1_eq, comparator_2_eq, comparator_3_eq, comparator_4_eq, not_1_out,
       not_2_out, WrReg0, WrReg1, WrReg2, WrReg3, WrReg4, WrReg5, WrReg6, WrReg7, WrReg8, WrReg9, WrReg10,
       WrReg11, WrReg12, WrReg13, WrReg14, WrReg15, WrReg16, WrReg17, WrReg18, WrReg19, WrReg20, WrReg21,
       WrReg22, WrReg23, WrReg24, WrReg25, WrReg26, WrReg27, WrReg28, WrReg29, WrReg30, WrReg31;
  wire [31:0] multiplexer_1_out, multiplexer_2_out, RegData1, RegData2, RegData3, RegData4, RegData5,
       RegData6, RegData7, RegData8, RegData9, RegData10, RegData11, RegData12, RegData13, RegData14,
       RegData15, RegData16, RegData17, RegData18, RegData19, RegData20, RegData21, RegData22, RegData23,
       RegData24, RegData25, RegData26, RegData27, RegData28, RegData29, RegData30, RegData31;

  Demultiplexer #(.select(5), .enable("false")) demultiplexer_1 (
    .out0(WrReg0), .out1(WrReg1), .out2(WrReg2), .out3(WrReg3), .out4(WrReg4), .out5(WrReg5), .out6(WrReg6),
    .out7(WrReg7), .out8(WrReg8), .out9(WrReg9), .out10(WrReg10), .out11(WrReg11), .out12(WrReg12),
    .out13(WrReg13), .out14(WrReg14), .out15(WrReg15), .out16(WrReg16), .out17(WrReg17), .out18(WrReg18),
    .out19(WrReg19), .out20(WrReg20), .out21(WrReg21), .out22(WrReg22), .out23(WrReg23), .out24(WrReg24),
    .out25(WrReg25), .out26(WrReg26), .out27(WrReg27), .out28(WrReg28), .out29(WrReg29), .out30(WrReg30),
    .out31(WrReg31), .in(WrReg), .sel(WrAddr));
  // Probe on RegData4
  Register #(.width(32)) Reg4 (.D(WrData), .en(WrReg4), .Q(RegData4), .clk(Clock));  // open: clr
  // Probe on RegData8
  Register #(.width(32)) Reg8 (.D(WrData), .en(WrReg8), .Q(RegData8), .clk(Clock));  // open: clr
  // Probe on RegData12
  Register #(.width(32)) Reg12 (.D(WrData), .en(WrReg12), .Q(RegData12), .clk(Clock));  // open: clr
  // Probe on RegData16
  Register #(.width(32)) Reg16 (.D(WrData), .en(WrReg16), .Q(RegData16), .clk(Clock));  // open: clr
  // Probe on RegData20
  Register #(.width(32)) Reg20 (.D(WrData), .en(WrReg20), .Q(RegData20), .clk(Clock));  // open: clr
  // Probe on RegData24
  Register #(.width(32)) Reg24 (.D(WrData), .en(WrReg24), .Q(RegData24), .clk(Clock));  // open: clr
  // Probe on RegData28
  Register #(.width(32)) Reg28 (.D(WrData), .en(WrReg28), .Q(RegData28), .clk(Clock));  // open: clr
  Register #(.width(32)) Reg1 (.D(WrData), .en(WrReg1), .Q(RegData1), .clk(Clock));  // open: clr
  Register #(.width(32)) Reg5 (.D(WrData), .en(WrReg5), .Q(RegData5), .clk(Clock));  // open: clr
  Register #(.width(32)) Reg9 (.D(WrData), .en(WrReg9), .Q(RegData9), .clk(Clock));  // open: clr
  Register #(.width(32)) Reg13 (.D(WrData), .en(WrReg13), .Q(RegData13), .clk(Clock));  // open: clr
  Register #(.width(32)) Reg17 (.D(WrData), .en(WrReg17), .Q(RegData17), .clk(Clock));  // open: clr
  Register #(.width(32)) Reg21 (.D(WrData), .en(WrReg21), .Q(RegData21), .clk(Clock));  // open: clr
  Register #(.width(32)) Reg25 (.D(WrData), .en(WrReg25), .Q(RegData25), .clk(Clock));  // open: clr
  Register #(.width(32)) Reg29 (.D(WrData), .en(WrReg29), .Q(RegData29), .clk(Clock));  // open: clr
  // Probe on RegData1
  // Probe on RegData5
  // Probe on RegData9
  // Probe on RegData13
  // Probe on RegData17
  // Probe on RegData21
  // Probe on RegData25
  // Probe on RegData29
  // Probe on RegData2
  Register #(.width(32)) Reg2 (.D(WrData), .en(WrReg2), .Q(RegData2), .clk(Clock));  // open: clr
  // Probe on RegData6
  Register #(.width(32)) Reg6 (.D(WrData), .en(WrReg6), .Q(RegData6), .clk(Clock));  // open: clr
  // Probe on RegData10
  Register #(.width(32)) Reg10 (.D(WrData), .en(WrReg10), .Q(RegData10), .clk(Clock));  // open: clr
  // Probe on RegData14
  Register #(.width(32)) Reg14 (.D(WrData), .en(WrReg14), .Q(RegData14), .clk(Clock));  // open: clr
  // Probe on RegData18
  Register #(.width(32)) Reg18 (.D(WrData), .en(WrReg18), .Q(RegData18), .clk(Clock));  // open: clr
  // Probe on RegData22
  Register #(.width(32)) Reg22 (.D(WrData), .en(WrReg22), .Q(RegData22), .clk(Clock));  // open: clr
  // Probe on RegData26
  Register #(.width(32)) Reg26 (.D(WrData), .en(WrReg26), .Q(RegData26), .clk(Clock));  // open: clr
  // Probe on RegData30
  Register #(.width(32)) Reg30 (.D(WrData), .en(WrReg30), .Q(RegData30), .clk(Clock));  // open: clr
  // Probe on RegData3
  Register #(.width(32)) Reg3 (.D(WrData), .en(WrReg3), .Q(RegData3), .clk(Clock));  // open: clr
  // Probe on RegData7
  Register #(.width(32)) Reg7 (.D(WrData), .en(WrReg7), .Q(RegData7), .clk(Clock));  // open: clr
  // Probe on RegData11
  Register #(.width(32)) Reg11 (.D(WrData), .en(WrReg11), .Q(RegData11), .clk(Clock));  // open: clr
  // Probe on RegData15
  Register #(.width(32)) Reg15 (.D(WrData), .en(WrReg15), .Q(RegData15), .clk(Clock));  // open: clr
  // Probe on RegData19
  Register #(.width(32)) Reg19 (.D(WrData), .en(WrReg19), .Q(RegData19), .clk(Clock));  // open: clr
  // Probe on RegData23
  Register #(.width(32)) Reg23 (.D(WrData), .en(WrReg23), .Q(RegData23), .clk(Clock));  // open: clr
  // Probe on RegData27
  Register #(.width(32)) Reg27 (.D(WrData), .en(WrReg27), .Q(RegData27), .clk(Clock));  // open: clr
  // Probe on RegData31
  Register #(.width(32)) Reg31 (.D(WrData), .en(WrReg31), .Q(RegData31), .clk(Clock));  // open: clr
  Multiplexer #(.select(5), .width(32), .enable("false")) multiplexer_1 (
    .in0({32{1'b0}}), .in1(RegData1), .in2(RegData2), .in3(RegData3), .in4(RegData4), .in5(RegData5),
    .in6(RegData6), .in7(RegData7), .in8(RegData8), .in9(RegData9), .in10(RegData10), .in11(RegData11),
    .in12(RegData12), .in13(RegData13), .in14(RegData14), .in15(RegData15), .in16(RegData16),
    .in17(RegData17), .in18(RegData18), .in19(RegData19), .in20(RegData20), .in21(RegData21),
    .in22(RegData22), .in23(RegData23), .in24(RegData24), .in25(RegData25), .in26(RegData26),
    .in27(RegData27), .in28(RegData28), .in29(RegData29), .in30(RegData30), .in31(RegData31),
    .out(multiplexer_1_out), .sel(RdAddr1));
  Multiplexer #(.select(5), .width(32), .enable("false")) multiplexer_2 (
    .in0({32{1'b0}}), .in1(RegData1), .in2(RegData2), .in3(RegData3), .in4(RegData4), .in5(RegData5),
    .in6(RegData6), .in7(RegData7), .in8(RegData8), .in9(RegData9), .in10(RegData10), .in11(RegData11),
    .in12(RegData12), .in13(RegData13), .in14(RegData14), .in15(RegData15), .in16(RegData16),
    .in17(RegData17), .in18(RegData18), .in19(RegData19), .in20(RegData20), .in21(RegData21),
    .in22(RegData22), .in23(RegData23), .in24(RegData24), .in25(RegData25), .in26(RegData26),
    .in27(RegData27), .in28(RegData28), .in29(RegData29), .in30(RegData30), .in31(RegData31),
    .out(multiplexer_2_out), .sel(RdAddr2));
  Multiplexer #(.width(32), .enable("false")) multiplexer_3 (
    .in0(multiplexer_1_out), .in1(WrData), .out(RdData1), .sel(and_1_out));
  Comparator #(.width(5), .mode("unsigned")) comparator_1 (
    .a(WrAddr), .b(RdAddr2), .eq(comparator_1_eq));  // open: gt, lt
  Multiplexer #(.width(32), .enable("false")) multiplexer_4 (
    .in0(multiplexer_2_out), .in1(WrData), .out(RdData2), .sel(and_2_out));
  Comparator #(.width(5), .mode("unsigned")) comparator_2 (
    .a(WrAddr), .b(RdAddr1), .eq(comparator_2_eq));  // open: gt, lt
  and and_1 (and_1_out, comparator_2_eq, WrReg, not_1_out);
  and and_2 (and_2_out, comparator_1_eq, WrReg, not_2_out);
  Comparator #(.width(5), .mode("unsigned")) comparator_3 (
    .a(WrAddr), .b({5{1'b0}}), .eq(comparator_3_eq));  // open: gt, lt
  not not_1 (not_1_out, comparator_3_eq);
  Comparator #(.width(5), .mode("unsigned")) comparator_4 (
    .a(WrAddr), .b({5{1'b0}}), .eq(comparator_4_eq));  // open: gt, lt
  not not_2 (not_2_out, comparator_4_eq);
endmodule

module Overflow_Unit (
  input  Add,
  input  Sub,
  input  ASign,
  input  BSign,
  input  ResultSign,
  output Overflow
);

  wire and_1_out, and_2_out, or_1_out, xnor_1_out, xor_1_out, xor_2_out;

  xnor xnor_1 (xnor_1_out, ASign, BSign);
  xor xor_1 (xor_1_out, ASign, BSign);
  and and_1 (and_1_out, xnor_1_out, Add);
  and and_2 (and_2_out, xor_1_out, Sub);
  or or_1 (or_1_out, and_1_out, and_2_out);
  xor xor_2 (xor_2_out, ResultSign, ASign);
  and and_3 (Overflow, or_1_out, xor_2_out);

  // Notes on the sheet:
  //   Overflow occurs when doing addition and sign(A) == sign(B) && sign(result) != sign(A)
  //   Or
  //   Overflow occurs when doing subtraction and sign(A) != sign(B) && sign(result) != sign(A)
endmodule

module ControlUnit (
  input  [31:0] InstructionIN,
  output [13:0] out_2
);

  wire or_1_out;
  wire [13:0] rom_1_data, rom_2_data;

  ROM #(.addrWidth(6), .dataWidth(14)) rom_1 (.addr(InstructionIN[5:0]), .data(rom_1_data));  // open: sel
  ROM #(.addrWidth(6), .dataWidth(14)) rom_2 (.addr(InstructionIN[31:26]), .data(rom_2_data));  // open: sel
  or or_1 (or_1_out, InstructionIN[26], InstructionIN[27], InstructionIN[28], InstructionIN[29], InstructionIN[30], InstructionIN[31]);
  Multiplexer #(.width(14)) multiplexer_1 (
    .in0(rom_1_data), .in1(rom_2_data), .out(out_2), .sel(or_1_out));  // open: en

  // Notes on the sheet:
  //   contents of rom_1 (hex, n*v repeats v):
  //   1071 0 1079 5*0 1c01 23*0 1001 0 1009 0 1011 1019 1029 1021 0 0 1031
  //   contents of rom_2 (hex, n*v repeats v):
  //   0 0 2802 2b03 408 0 0 0 3 0 0 0 13 1b 21*0 283 7*0 6
endmodule

module _1 (
);

  ROM #(.addrWidth(6), .dataWidth(14)) rom_1 ();  // open: addr, data, sel

  // Notes on the sheet:
  //   contents of rom_1 (hex, n*v repeats v):
  //   1071 0 1079 5*0 1831 23*0 1001 0 1009 0 1011 1019 1029 1021 0 0 1031
endmodule

module _2 (
  input  Op5,
  input  Op4,
  input  Op3,
  input  Op2,
  input  Op1,
  input  Op0,
  output RegDst0,
  output RegDst,
  output WrReg,
  output ALUSrc,
  output ALUC3,
  output ALUC2,
  output ALUC1,
  output ALUC0,
  output MemWr,
  output MemToReg0,
  output MemToReg,
  output JUMP
);

  wire and_1_out, and_2_out, and_3_out, and_4_out, and_5_out, and_8_out, and_9_out, and_10_out, and_11_out,
       and_12_out, and_13_out, and_14_out, and_15_out, and_16_out, and_17_out, and_18_out, and_19_out,
       and_20_out, and_21_out, and_23_out, and_24_out, and_25_out, and_26_out, and_27_out, not_1_out,
       not_2_out, not_3_out, not_4_out, not_5_out, not_6_out, not_7_out, not_8_out, not_9_out, not_10_out,
       not_11_out, not_12_out, not_13_out, not_14_out, not_15_out, not_16_out, not_17_out, not_18_out,
       not_19_out, not_20_out, not_21_out, not_22_out, not_23_out, not_24_out, not_25_out, not_26_out,
       not_27_out, not_28_out, not_29_out, not_30_out, not_31_out, not_32_out, not_33_out, not_34_out,
       not_35_out, not_36_out, not_37_out, not_38_out, not_39_out, not_40_out, not_41_out, not_42_out,
       not_43_out, not_44_out, not_45_out;

  not not_1 (not_1_out, Op5);
  not not_2 (not_2_out, Op4);
  not not_3 (not_3_out, Op3);
  not not_4 (not_4_out, Op2);
  not not_5 (not_5_out, Op5);
  not not_6 (not_6_out, Op4);
  not not_7 (not_7_out, Op3);
  not not_8 (not_8_out, Op1);
  not not_9 (not_9_out, Op0);
  not not_10 (not_10_out, Op2);
  not not_11 (not_11_out, Op1);
  not not_12 (not_12_out, Op3);
  not not_13 (not_13_out, Op3);
  not not_14 (not_14_out, Op1);
  not not_15 (not_15_out, Op3);
  not not_16 (not_16_out, Op3);
  not not_17 (not_17_out, Op2);
  and and_1 (and_1_out, Op2, Op0);
  and and_2 (and_2_out, Op2, Op1);
  and and_3 (and_3_out, Op3, Op2);
  and and_4 (and_4_out, Op4, Op2);
  and and_5 (and_5_out, Op5, Op2);
  not not_18 (not_18_out, Op1);
  not not_19 (not_19_out, Op5);
  not not_20 (not_20_out, Op4);
  not not_21 (not_21_out, Op3);
  not not_22 (not_22_out, Op1);
  not not_23 (not_23_out, Op2);
  not not_24 (not_24_out, Op1);
  not not_25 (not_25_out, Op3);
  not not_26 (not_26_out, Op0);
  not not_27 (not_27_out, Op3);
  not not_28 (not_28_out, Op1);
  not not_29 (not_29_out, Op3);
  not not_30 (not_30_out, Op3);
  not not_31 (not_31_out, Op5);
  not not_32 (not_32_out, Op4);
  not not_33 (not_33_out, Op3);
  not not_34 (not_34_out, Op2);
  not not_35 (not_35_out, Op3);
  not not_36 (not_36_out, Op1);
  not not_37 (not_37_out, Op3);
  not not_38 (not_38_out, Op0);
  not not_39 (not_39_out, Op3);
  not not_40 (not_40_out, Op3);
  not not_41 (not_41_out, Op3);
  not not_42 (not_42_out, Op5);
  not not_43 (not_43_out, Op4);
  not not_44 (not_44_out, Op3);
  not not_45 (not_45_out, Op2);
  and and_6 (RegDst0, not_1_out, not_2_out, not_3_out, not_4_out, Op1);
  and and_7 (RegDst, not_5_out, not_6_out, not_7_out, Op2, not_8_out, not_9_out);
  and and_8 (and_8_out, not_10_out, not_11_out);
  and and_9 (and_9_out, not_12_out, Op0);
  and and_10 (and_10_out, not_13_out, Op2, Op1);
  and and_11 (and_11_out, Op3, not_14_out);
  and and_12 (and_12_out, Op4, not_15_out);
  and and_13 (and_13_out, Op5, not_16_out);
  or or_1 (ALUSrc, not_17_out, Op0, Op1, Op3, Op4, Op5);
  or or_2 (ALUC1, and_1_out, and_2_out, and_3_out, and_4_out, and_5_out);
  and and_14 (and_14_out, not_18_out, Op0);
  and and_15 (and_15_out, not_19_out, not_20_out, not_21_out, Op2, not_22_out);
  and and_16 (and_16_out, not_23_out, not_24_out);
  and and_17 (and_17_out, not_25_out, Op1, not_26_out);
  and and_18 (and_18_out, not_27_out, Op2, Op0);
  and and_19 (and_19_out, Op3, not_28_out);
  and and_20 (and_20_out, Op4, not_29_out);
  and and_21 (and_21_out, Op5, not_30_out);
  and and_22 (MemToReg0, not_31_out, not_32_out, not_33_out, not_34_out, Op1, Op0);
  and and_23 (and_23_out, not_35_out, not_36_out);
  and and_24 (and_24_out, not_37_out, not_38_out);
  and and_25 (and_25_out, not_39_out, Op2);
  and and_26 (and_26_out, Op4, not_40_out);
  and and_27 (and_27_out, Op5, not_41_out);
  and and_28 (JUMP, not_42_out, not_43_out, not_44_out, not_45_out, Op1);
  or or_3 (WrReg, and_8_out, and_9_out, and_10_out, and_11_out, and_12_out, and_13_out);
  or or_4 (ALUC0, and_14_out, and_15_out);
  or or_5 (MemWr, and_16_out, and_17_out, and_18_out, and_19_out, and_20_out, and_21_out);
  or or_6 (MemToReg, and_23_out, and_24_out, and_25_out, and_26_out, and_27_out);

  assign ALUC2 = 1'b0;
  assign ALUC3 = 1'b0;
endmodule

module Forwarding_Unit (
  input  EX_MEM_RegWrite,
  input  [4:0] EX_MEM_RegisterRd,
  input  [4:0] ID_EX_RegisterRs,
  input  MEM_WB_RegWrite,
  input  [4:0] MEM_WB_RegisterRd,
  input  [4:0] ID_EX_RegisterRt,
  output [1:0] ForwardA,
  output [1:0] ForwardB
);

  wire and_1_out, and_2_out, and_3_out, and_4_out, and_5_out, and_9_out, and_11_out, and_12_out, or_1_out,
       or_2_out, or_3_out, or_4_out, or_5_out, or_6_out;
  wire [1:0] and_8_out, and_10_out;
  wire [4:0] xnor_1_out, xnor_2_out, xnor_3_out, xnor_4_out, xnor_5_out, xnor_6_out, xor_1_out, xor_2_out,
       xor_3_out, xor_4_out, xor_5_out, xor_6_out;

  assign xnor_1_out = ~(EX_MEM_RegisterRd ^ ID_EX_RegisterRs);  // XNOR_Gate xnor_1, 5 bits wide
  assign xor_1_out = EX_MEM_RegisterRd ^ {5{1'b0}};  // XOR_Gate xor_1, 5 bits wide
  assign xnor_2_out = ~(MEM_WB_RegisterRd ^ ID_EX_RegisterRs);  // XNOR_Gate xnor_2, 5 bits wide
  assign xor_2_out = MEM_WB_RegisterRd ^ {5{1'b0}};  // XOR_Gate xor_2, 5 bits wide
  assign xnor_3_out = ~(EX_MEM_RegisterRd ^ ID_EX_RegisterRt);  // XNOR_Gate xnor_3, 5 bits wide
  assign xor_3_out = EX_MEM_RegisterRd ^ {5{1'b0}};  // XOR_Gate xor_3, 5 bits wide
  assign xnor_4_out = ~(MEM_WB_RegisterRd ^ ID_EX_RegisterRt);  // XNOR_Gate xnor_4, 5 bits wide
  assign xor_4_out = MEM_WB_RegisterRd ^ {5{1'b0}};  // XOR_Gate xor_4, 5 bits wide
  assign xor_5_out = EX_MEM_RegisterRd ^ {5{1'b0}};  // XOR_Gate xor_5, 5 bits wide
  assign xnor_5_out = ~(EX_MEM_RegisterRd ^ ID_EX_RegisterRt);  // XNOR_Gate xnor_5, 5 bits wide
  and and_1 (and_1_out, xnor_1_out[0], xnor_1_out[1], xnor_1_out[2], xnor_1_out[3], xnor_1_out[4]);
  or or_1 (or_1_out, xor_1_out[0], xor_1_out[1], xor_1_out[2], xor_1_out[3], xor_1_out[4]);
  and and_2 (and_2_out, xnor_2_out[0], xnor_2_out[1], xnor_2_out[2], xnor_2_out[3], xnor_2_out[4]);
  or or_2 (or_2_out, xor_2_out[0], xor_2_out[1], xor_2_out[2], xor_2_out[3], xor_2_out[4]);
  assign xor_6_out = EX_MEM_RegisterRd ^ {5{1'b0}};  // XOR_Gate xor_6, 5 bits wide
  assign xnor_6_out = ~(EX_MEM_RegisterRd ^ ID_EX_RegisterRs);  // XNOR_Gate xnor_6, 5 bits wide
  and and_3 (and_3_out, xnor_3_out[0], xnor_3_out[1], xnor_3_out[2], xnor_3_out[3], xnor_3_out[4]);
  or or_3 (or_3_out, xor_3_out[0], xor_3_out[1], xor_3_out[2], xor_3_out[3], xor_3_out[4]);
  and and_4 (and_4_out, xnor_4_out[0], xnor_4_out[1], xnor_4_out[2], xnor_4_out[3], xnor_4_out[4]);
  or or_4 (or_4_out, xor_4_out[0], xor_4_out[1], xor_4_out[2], xor_4_out[3], xor_4_out[4]);
  or or_5 (or_5_out, xor_5_out[0], xor_5_out[1], xor_5_out[2], xor_5_out[3], xor_5_out[4]);
  and and_5 (and_5_out, xnor_5_out[0], xnor_5_out[1], xnor_5_out[2], xnor_5_out[3], xnor_5_out[4]);
  and and_6 (and_8_out[1], EX_MEM_RegWrite, and_1_out, or_1_out);
  and and_7 (and_10_out[1], EX_MEM_RegWrite, and_3_out, or_3_out);
  and and_8 (and_8_out[0], MEM_WB_RegWrite, or_2_out, and_2_out, ~and_12_out);  // AND_Gate
  or or_6 (or_6_out, xor_6_out[0], xor_6_out[1], xor_6_out[2], xor_6_out[3], xor_6_out[4]);
  and and_9 (and_9_out, xnor_6_out[0], xnor_6_out[1], xnor_6_out[2], xnor_6_out[3], xnor_6_out[4]);
  and and_10 (and_10_out[0], MEM_WB_RegWrite, or_4_out, and_4_out, ~and_11_out);  // AND_Gate
  and and_11 (and_11_out, EX_MEM_RegWrite, or_5_out, and_5_out);
  and and_12 (and_12_out, EX_MEM_RegWrite, or_6_out, and_9_out);
  Multiplexer #(.select(2), .width(2)) multiplexer_1 (
    .in0(2'b00), .in1(2'b01), .in2(2'b10), .out(ForwardA), .sel(and_8_out));  // open: in3, en
  Multiplexer #(.select(2), .width(2)) multiplexer_2 (
    .in0(2'b00), .in1(2'b01), .in2(2'b10), .out(ForwardB), .sel(and_10_out));  // open: in3, en
endmodule

module IF_ID (
  input  [31:0] PC_4,
  input  [31:0] PC,
  input  Stall,
  input  Clock,
  input  Branch,
  output [31:0] PC_4out,
  output [31:0] INSTout
);

  Register #(.width(32)) u_PC_4 (.D(PC_4), .en(Stall), .Q(PC_4out), .clk(Clock), .clr(Branch));
  Register #(.width(32)) Inst (.D(PC), .en(Stall), .Q(INSTout), .clk(Clock), .clr(Branch));
endmodule

module ID_EX (
  input  ALUSrc,
  input  [3:0] ALUControl,
  input  [1:0] MemToReg,
  input  Branch,
  input  Jump,
  input  [31:0] Inst,
  input  [31:0] ID_PC,
  input  [31:0] ID_PC_2,
  input  [31:0] RdData1,
  input  [31:0] RdData2,
  input  [31:0] instImm,
  input  [4:0] rd,
  input  [4:0] rt,
  input  [4:0] rs,
  input  RegWrite,
  input  MemWrite,
  input  MemRead,
  input  [1:0] RegDst,
  input  [4:0] shamt,
  input  Clock,
  input  Clear,
  output out_22,
  output [3:0] out_23,
  output [1:0] out_24,
  output out_25,
  output out_26,
  output [31:0] out_27,
  output [31:0] out_28,
  output [31:0] out_29,
  output [31:0] out_30,
  output [31:0] out_31,
  output [31:0] out_32,
  output [4:0] out_33,
  output [4:0] out_34,
  output [4:0] out_35,
  output out_36,
  output out_37,
  output out_38,
  output [1:0] RegDstF,
  output [4:0] out_40
);

  Register #(.width(1)) register_1 (.D(ALUSrc), .Q(out_22), .clk(Clock), .clr(Clear));  // open: en
  Register #(.width(4)) register_2 (.D(ALUControl), .Q(out_23), .clk(Clock), .clr(Clear));  // open: en
  Register #(.width(2)) register_3 (.D(MemToReg), .Q(out_24), .clk(Clock), .clr(Clear));  // open: en
  Register #(.width(1)) register_4 (.D(Branch), .Q(out_25), .clk(Clock), .clr(Clear));  // open: en
  Register #(.width(1)) register_5 (.D(Jump), .Q(out_26), .clk(Clock), .clr(Clear));  // open: en
  Register #(.width(32)) register_6 (.D(Inst), .Q(out_27), .clk(Clock), .clr(Clear));  // open: en
  Register #(.width(32)) register_7 (.D(ID_PC), .Q(out_28), .clk(Clock), .clr(Clear));  // open: en
  Register #(.width(32)) register_8 (.D(ID_PC_2), .Q(out_29), .clk(Clock), .clr(Clear));  // open: en
  Register #(.width(32)) A (.D(RdData1), .Q(out_30), .clk(Clock), .clr(Clear));  // open: en
  Register #(.width(32)) B (.D(RdData2), .Q(out_31), .clk(Clock), .clr(Clear));  // open: en
  Register #(.width(32)) imm (.D(instImm), .Q(out_32), .clk(Clock), .clr(Clear));  // open: en
  Register #(.width(5)) u_Rd (.D(rd), .Q(out_33), .clk(Clock), .clr(Clear));  // open: en
  Register #(.width(5)) u_Rt (.D(rt), .Q(out_34), .clk(Clock), .clr(Clear));  // open: en
  Register #(.width(5)) u_Rs (.D(rs), .Q(out_35), .clk(Clock), .clr(Clear));  // open: en
  Register #(.width(1)) EX_RegWrite (.D(RegWrite), .Q(out_36), .clk(Clock), .clr(Clear));  // open: en
  Register #(.width(1)) EX_MemWR (.D(MemWrite), .Q(out_37), .clk(Clock), .clr(Clear));  // open: en
  Register #(.width(1)) EX_MemRd (.D(MemRead), .Q(out_38), .clk(Clock), .clr(Clear));  // open: en
  Register #(.width(2)) EX_RegDst (.D(RegDst), .Q(RegDstF), .clk(Clock), .clr(Clear));  // open: en
  Register #(.width(5)) u_SHAMT (.D(shamt), .Q(out_40), .clk(Clock), .clr(Clear));  // open: en
endmodule

module EX_MEM (
  input  [1:0] MemToReg,
  input  Branch,
  input  Jump,
  input  [31:0] Inst,
  input  [31:0] Ex_PC,
  input  [31:0] Ex_PC2,
  input  [4:0] Ex_WriteAddr,
  input  ALUZero,
  input  [31:0] Din,
  input  [31:0] Bin,
  input  RegWrite,
  input  MemWrite,
  input  MemRead,
  input  Clock,
  output [1:0] out_15,
  output out_16,
  output out_17,
  output [31:0] out_18,
  output [31:0] out_19,
  output [31:0] out_20,
  output [4:0] out_21,
  output out_22,
  output [31:0] out_23,
  output [31:0] out_24,
  output out_25,
  output out_26,
  output out_27
);

  Register #(.width(2)) register_1 (.D(MemToReg), .Q(out_15), .clk(Clock));  // open: en, clr
  Register #(.width(1)) register_2 (.D(Branch), .Q(out_16), .clk(Clock));  // open: en, clr
  Register #(.width(1)) register_3 (.D(Jump), .Q(out_17), .clk(Clock));  // open: en, clr
  Register #(.width(32)) register_4 (.D(Inst), .Q(out_18), .clk(Clock));  // open: en, clr
  Register #(.width(32)) register_5 (.D(Ex_PC), .Q(out_19), .clk(Clock));  // open: en, clr
  Register #(.width(32)) register_6 (.D(Ex_PC2), .Q(out_20), .clk(Clock));  // open: en, clr
  Register #(.width(5)) MEM_wrAddr (.D(Ex_WriteAddr), .Q(out_21), .clk(Clock));  // open: en, clr
  Register #(.width(1)) MEM_ALUzero (.D(ALUZero), .Q(out_22), .clk(Clock));  // open: en, clr
  Register #(.width(32)) D (.D(Din), .Q(out_23), .clk(Clock));  // open: en, clr
  Register #(.width(32)) B (.D(Bin), .Q(out_24), .clk(Clock));  // open: en, clr
  Register #(.width(1)) MEM_RegWrite (.D(RegWrite), .Q(out_25), .clk(Clock));  // open: en, clr
  Register #(.width(1)) MEM_MemWR (.D(MemWrite), .Q(out_26), .clk(Clock));  // open: en, clr
  Register #(.width(1)) MEM_MemRd (.D(MemRead), .Q(out_27), .clk(Clock));  // open: en, clr
endmodule

module MEM_WB (
  input  [1:0] MemToReg,
  input  [31:0] MEM_PC2,
  input  [4:0] MEM_WriteAddr,
  input  [31:0] Dout1,
  input  [31:0] Min,
  input  RegWrite,
  input  Clock,
  output [1:0] out_8,
  output [31:0] out_9,
  output [4:0] out_10,
  output [31:0] out_11,
  output [31:0] out_12,
  output out_13
);

  Register #(.width(2)) register_1 (.D(MemToReg), .Q(out_8), .clk(Clock));  // open: en, clr
  Register #(.width(32)) register_2 (.D(MEM_PC2), .Q(out_9), .clk(Clock));  // open: en, clr
  Register #(.width(5)) WB_wrAddr (.D(MEM_WriteAddr), .Q(out_10), .clk(Clock));  // open: en, clr
  Register #(.width(32)) D (.D(Dout1), .Q(out_11), .clk(Clock));  // open: en, clr
  Register #(.width(32)) M (.D(Min), .Q(out_12), .clk(Clock));  // open: en, clr
  Register #(.width(1)) WB_RegWrite (.D(RegWrite), .Q(out_13), .clk(Clock));  // open: en, clr
endmodule

module Hazard_Unit (
  input  ID_EX_MemRead,
  input  [4:0] ID_EX_RegisterRt,
  input  [4:0] IF_ID_RegisterRs,
  input  [4:0] IF_ID_RegisterRt,
  output Stall
);

  wire and_1_out, and_2_out, or_1_out;
  wire [4:0] xnor_1_out, xnor_2_out;

  assign xnor_1_out = ~(ID_EX_RegisterRt ^ IF_ID_RegisterRs);  // XNOR_Gate xnor_1, 5 bits wide
  assign xnor_2_out = ~(ID_EX_RegisterRt ^ IF_ID_RegisterRt);  // XNOR_Gate xnor_2, 5 bits wide
  and and_1 (and_1_out, xnor_1_out[0], xnor_1_out[1], xnor_1_out[2], xnor_1_out[3], xnor_1_out[4]);
  and and_2 (and_2_out, xnor_2_out[0], xnor_2_out[1], xnor_2_out[2], xnor_2_out[3], xnor_2_out[4]);
  or or_1 (or_1_out, and_1_out, and_2_out);
  and and_3 (Stall, ID_EX_MemRead, or_1_out);
endmodule

module JR (
  input  [5:0] Function,
  input  [4:0] Shiftamt,
  input  [4:0] rd,
  input  [4:0] rt,
  input  [5:0] Opcode,
  output JR
);

  and and_1 (JR, ~Function[5], ~Function[4], Function[3], ~Function[2], ~Function[1], ~Function[0], ~Shiftamt[4], ~Shiftamt[3], ~Shiftamt[2], ~Shiftamt[1], ~Shiftamt[0], ~rd[4], ~rd[3], ~rd[2], ~rd[1], ~rd[0], ~rt[4], ~rt[3], ~rt[2], ~rt[1], ~rt[0], ~Opcode[5], ~Opcode[4], ~Opcode[3], ~Opcode[2], ~Opcode[1], ~Opcode[0]);  // AND_Gate
endmodule
